// Digital circuit block_function.dig as structural Verilog
module block_function (
  input  [31:0] k0,
  input  [31:0] k1,
  input  [31:0] k2,
  input  [31:0] k3,
  input  [31:0] k4,
  input  [31:0] k5,
  input  [31:0] k6,
  input  [31:0] k7,
  input  [31:0] bc,
  input  [31:0] n0,
  input  [31:0] n1,
  input  [31:0] n2,
  output [31:0] o0,
  output [31:0] o1,
  output [31:0] o2,
  output [31:0] o3,
  output [31:0] o4,
  output [31:0] o5,
  output [31:0] o6,
  output [31:0] o7,
  output [31:0] o8,
  output [31:0] o9,
  output [31:0] o10,
  output [31:0] o11,
  output [31:0] o12,
  output [31:0] o13,
  output [31:0] o14,
  output [31:0] o15
);

  wire [31:0] inner_block_function_1__0_2, inner_block_function_1__1_2, inner_block_function_1__2_2,
       inner_block_function_1__3_2, inner_block_function_1__4_2, inner_block_function_1__5_2,
       inner_block_function_1__6_2, inner_block_function_1__7_2, inner_block_function_1__8_2,
       inner_block_function_1__9_2, inner_block_function_1__10_2, inner_block_function_1__11_2,
       inner_block_function_1__12_2, inner_block_function_1__13_2, inner_block_function_1__14_2,
       inner_block_function_1__15_2, inner_block_function_2__0_2, inner_block_function_2__1_2,
       inner_block_function_2__2_2, inner_block_function_2__3_2, inner_block_function_2__4_2,
       inner_block_function_2__5_2, inner_block_function_2__6_2, inner_block_function_2__7_2,
       inner_block_function_2__8_2, inner_block_function_2__9_2, inner_block_function_2__10_2,
       inner_block_function_2__11_2, inner_block_function_2__12_2, inner_block_function_2__13_2,
       inner_block_function_2__14_2, inner_block_function_2__15_2, inner_block_function_3__0_2,
       inner_block_function_3__1_2, inner_block_function_3__2_2, inner_block_function_3__3_2,
       inner_block_function_3__4_2, inner_block_function_3__5_2, inner_block_function_3__6_2,
       inner_block_function_3__7_2, inner_block_function_3__8_2, inner_block_function_3__9_2,
       inner_block_function_3__10_2, inner_block_function_3__11_2, inner_block_function_3__12_2,
       inner_block_function_3__13_2, inner_block_function_3__14_2, inner_block_function_3__15_2,
       inner_block_function_4__0_2, inner_block_function_4__1_2, inner_block_function_4__2_2,
       inner_block_function_4__3_2, inner_block_function_4__4_2, inner_block_function_4__5_2,
       inner_block_function_4__6_2, inner_block_function_4__7_2, inner_block_function_4__8_2,
       inner_block_function_4__9_2, inner_block_function_4__10_2, inner_block_function_4__11_2,
       inner_block_function_4__12_2, inner_block_function_4__13_2, inner_block_function_4__14_2,
       inner_block_function_4__15_2, inner_block_function_5__0_2, inner_block_function_5__1_2,
       inner_block_function_5__2_2, inner_block_function_5__3_2, inner_block_function_5__4_2,
       inner_block_function_5__5_2, inner_block_function_5__6_2, inner_block_function_5__7_2,
       inner_block_function_5__8_2, inner_block_function_5__9_2, inner_block_function_5__10_2,
       inner_block_function_5__11_2, inner_block_function_5__12_2, inner_block_function_5__13_2,
       inner_block_function_5__14_2, inner_block_function_5__15_2, inner_block_function_6__0_2,
       inner_block_function_6__1_2, inner_block_function_6__2_2, inner_block_function_6__3_2,
       inner_block_function_6__4_2, inner_block_function_6__5_2, inner_block_function_6__6_2,
       inner_block_function_6__7_2, inner_block_function_6__8_2, inner_block_function_6__9_2,
       inner_block_function_6__10_2, inner_block_function_6__11_2, inner_block_function_6__12_2,
       inner_block_function_6__13_2, inner_block_function_6__14_2, inner_block_function_6__15_2,
       inner_block_function_7__0_2, inner_block_function_7__1_2, inner_block_function_7__2_2,
       inner_block_function_7__3_2, inner_block_function_7__4_2, inner_block_function_7__5_2,
       inner_block_function_7__6_2, inner_block_function_7__7_2, inner_block_function_7__8_2,
       inner_block_function_7__9_2, inner_block_function_7__10_2, inner_block_function_7__11_2,
       inner_block_function_7__12_2, inner_block_function_7__13_2, inner_block_function_7__14_2,
       inner_block_function_7__15_2, inner_block_function_8__0_2, inner_block_function_8__1_2,
       inner_block_function_8__2_2, inner_block_function_8__3_2, inner_block_function_8__4_2,
       inner_block_function_8__5_2, inner_block_function_8__6_2, inner_block_function_8__7_2,
       inner_block_function_8__8_2, inner_block_function_8__9_2, inner_block_function_8__10_2,
       inner_block_function_8__11_2, inner_block_function_8__12_2, inner_block_function_8__13_2,
       inner_block_function_8__14_2, inner_block_function_8__15_2, inner_block_function_9__0_2,
       inner_block_function_9__1_2, inner_block_function_9__2_2, inner_block_function_9__3_2,
       inner_block_function_9__4_2, inner_block_function_9__5_2, inner_block_function_9__6_2,
       inner_block_function_9__7_2, inner_block_function_9__8_2, inner_block_function_9__9_2,
       inner_block_function_9__10_2, inner_block_function_9__11_2, inner_block_function_9__12_2,
       inner_block_function_9__13_2, inner_block_function_9__14_2, inner_block_function_9__15_2;

  inner_block_function inner_block_function_1 (
    ._0(32'h61707865), ._1(32'h3320646e), ._2(32'h79622d32), ._3(32'h6b206574), ._4(k0), ._5(k1), ._6(k2),
    ._7(k3), ._8(k4), ._9(k5), ._10(k6), ._11(k7), ._12(bc), ._13(n0), ._14(n1), ._15(n2),
    ._0_2(inner_block_function_1__0_2), ._1_2(inner_block_function_1__1_2),
    ._2_2(inner_block_function_1__2_2), ._3_2(inner_block_function_1__3_2),
    ._4_2(inner_block_function_1__4_2), ._5_2(inner_block_function_1__5_2),
    ._6_2(inner_block_function_1__6_2), ._7_2(inner_block_function_1__7_2),
    ._8_2(inner_block_function_1__8_2), ._9_2(inner_block_function_1__9_2),
    ._10_2(inner_block_function_1__10_2), ._11_2(inner_block_function_1__11_2),
    ._12_2(inner_block_function_1__12_2), ._13_2(inner_block_function_1__13_2),
    ._14_2(inner_block_function_1__14_2), ._15_2(inner_block_function_1__15_2));
  inner_block_function inner_block_function_2 (
    ._0(inner_block_function_1__0_2), ._1(inner_block_function_1__1_2), ._2(inner_block_function_1__2_2),
    ._3(inner_block_function_1__3_2), ._4(inner_block_function_1__4_2), ._5(inner_block_function_1__5_2),
    ._6(inner_block_function_1__6_2), ._7(inner_block_function_1__7_2), ._8(inner_block_function_1__8_2),
    ._9(inner_block_function_1__9_2), ._10(inner_block_function_1__10_2), ._11(inner_block_function_1__11_2),
    ._12(inner_block_function_1__12_2), ._13(inner_block_function_1__13_2),
    ._14(inner_block_function_1__14_2), ._15(inner_block_function_1__15_2),
    ._0_2(inner_block_function_2__0_2), ._1_2(inner_block_function_2__1_2),
    ._2_2(inner_block_function_2__2_2), ._3_2(inner_block_function_2__3_2),
    ._4_2(inner_block_function_2__4_2), ._5_2(inner_block_function_2__5_2),
    ._6_2(inner_block_function_2__6_2), ._7_2(inner_block_function_2__7_2),
    ._8_2(inner_block_function_2__8_2), ._9_2(inner_block_function_2__9_2),
    ._10_2(inner_block_function_2__10_2), ._11_2(inner_block_function_2__11_2),
    ._12_2(inner_block_function_2__12_2), ._13_2(inner_block_function_2__13_2),
    ._14_2(inner_block_function_2__14_2), ._15_2(inner_block_function_2__15_2));
  inner_block_function inner_block_function_3 (
    ._0(inner_block_function_2__0_2), ._1(inner_block_function_2__1_2), ._2(inner_block_function_2__2_2),
    ._3(inner_block_function_2__3_2), ._4(inner_block_function_2__4_2), ._5(inner_block_function_2__5_2),
    ._6(inner_block_function_2__6_2), ._7(inner_block_function_2__7_2), ._8(inner_block_function_2__8_2),
    ._9(inner_block_function_2__9_2), ._10(inner_block_function_2__10_2), ._11(inner_block_function_2__11_2),
    ._12(inner_block_function_2__12_2), ._13(inner_block_function_2__13_2),
    ._14(inner_block_function_2__14_2), ._15(inner_block_function_2__15_2),
    ._0_2(inner_block_function_3__0_2), ._1_2(inner_block_function_3__1_2),
    ._2_2(inner_block_function_3__2_2), ._3_2(inner_block_function_3__3_2),
    ._4_2(inner_block_function_3__4_2), ._5_2(inner_block_function_3__5_2),
    ._6_2(inner_block_function_3__6_2), ._7_2(inner_block_function_3__7_2),
    ._8_2(inner_block_function_3__8_2), ._9_2(inner_block_function_3__9_2),
    ._10_2(inner_block_function_3__10_2), ._11_2(inner_block_function_3__11_2),
    ._12_2(inner_block_function_3__12_2), ._13_2(inner_block_function_3__13_2),
    ._14_2(inner_block_function_3__14_2), ._15_2(inner_block_function_3__15_2));
  inner_block_function inner_block_function_4 (
    ._0(inner_block_function_3__0_2), ._1(inner_block_function_3__1_2), ._2(inner_block_function_3__2_2),
    ._3(inner_block_function_3__3_2), ._4(inner_block_function_3__4_2), ._5(inner_block_function_3__5_2),
    ._6(inner_block_function_3__6_2), ._7(inner_block_function_3__7_2), ._8(inner_block_function_3__8_2),
    ._9(inner_block_function_3__9_2), ._10(inner_block_function_3__10_2), ._11(inner_block_function_3__11_2),
    ._12(inner_block_function_3__12_2), ._13(inner_block_function_3__13_2),
    ._14(inner_block_function_3__14_2), ._15(inner_block_function_3__15_2),
    ._0_2(inner_block_function_4__0_2), ._1_2(inner_block_function_4__1_2),
    ._2_2(inner_block_function_4__2_2), ._3_2(inner_block_function_4__3_2),
    ._4_2(inner_block_function_4__4_2), ._5_2(inner_block_function_4__5_2),
    ._6_2(inner_block_function_4__6_2), ._7_2(inner_block_function_4__7_2),
    ._8_2(inner_block_function_4__8_2), ._9_2(inner_block_function_4__9_2),
    ._10_2(inner_block_function_4__10_2), ._11_2(inner_block_function_4__11_2),
    ._12_2(inner_block_function_4__12_2), ._13_2(inner_block_function_4__13_2),
    ._14_2(inner_block_function_4__14_2), ._15_2(inner_block_function_4__15_2));
  inner_block_function inner_block_function_5 (
    ._0(inner_block_function_4__0_2), ._1(inner_block_function_4__1_2), ._2(inner_block_function_4__2_2),
    ._3(inner_block_function_4__3_2), ._4(inner_block_function_4__4_2), ._5(inner_block_function_4__5_2),
    ._6(inner_block_function_4__6_2), ._7(inner_block_function_4__7_2), ._8(inner_block_function_4__8_2),
    ._9(inner_block_function_4__9_2), ._10(inner_block_function_4__10_2), ._11(inner_block_function_4__11_2),
    ._12(inner_block_function_4__12_2), ._13(inner_block_function_4__13_2),
    ._14(inner_block_function_4__14_2), ._15(inner_block_function_4__15_2),
    ._0_2(inner_block_function_5__0_2), ._1_2(inner_block_function_5__1_2),
    ._2_2(inner_block_function_5__2_2), ._3_2(inner_block_function_5__3_2),
    ._4_2(inner_block_function_5__4_2), ._5_2(inner_block_function_5__5_2),
    ._6_2(inner_block_function_5__6_2), ._7_2(inner_block_function_5__7_2),
    ._8_2(inner_block_function_5__8_2), ._9_2(inner_block_function_5__9_2),
    ._10_2(inner_block_function_5__10_2), ._11_2(inner_block_function_5__11_2),
    ._12_2(inner_block_function_5__12_2), ._13_2(inner_block_function_5__13_2),
    ._14_2(inner_block_function_5__14_2), ._15_2(inner_block_function_5__15_2));
  inner_block_function inner_block_function_6 (
    ._0(inner_block_function_5__0_2), ._1(inner_block_function_5__1_2), ._2(inner_block_function_5__2_2),
    ._3(inner_block_function_5__3_2), ._4(inner_block_function_5__4_2), ._5(inner_block_function_5__5_2),
    ._6(inner_block_function_5__6_2), ._7(inner_block_function_5__7_2), ._8(inner_block_function_5__8_2),
    ._9(inner_block_function_5__9_2), ._10(inner_block_function_5__10_2), ._11(inner_block_function_5__11_2),
    ._12(inner_block_function_5__12_2), ._13(inner_block_function_5__13_2),
    ._14(inner_block_function_5__14_2), ._15(inner_block_function_5__15_2),
    ._0_2(inner_block_function_6__0_2), ._1_2(inner_block_function_6__1_2),
    ._2_2(inner_block_function_6__2_2), ._3_2(inner_block_function_6__3_2),
    ._4_2(inner_block_function_6__4_2), ._5_2(inner_block_function_6__5_2),
    ._6_2(inner_block_function_6__6_2), ._7_2(inner_block_function_6__7_2),
    ._8_2(inner_block_function_6__8_2), ._9_2(inner_block_function_6__9_2),
    ._10_2(inner_block_function_6__10_2), ._11_2(inner_block_function_6__11_2),
    ._12_2(inner_block_function_6__12_2), ._13_2(inner_block_function_6__13_2),
    ._14_2(inner_block_function_6__14_2), ._15_2(inner_block_function_6__15_2));
  inner_block_function inner_block_function_7 (
    ._0(inner_block_function_6__0_2), ._1(inner_block_function_6__1_2), ._2(inner_block_function_6__2_2),
    ._3(inner_block_function_6__3_2), ._4(inner_block_function_6__4_2), ._5(inner_block_function_6__5_2),
    ._6(inner_block_function_6__6_2), ._7(inner_block_function_6__7_2), ._8(inner_block_function_6__8_2),
    ._9(inner_block_function_6__9_2), ._10(inner_block_function_6__10_2), ._11(inner_block_function_6__11_2),
    ._12(inner_block_function_6__12_2), ._13(inner_block_function_6__13_2),
    ._14(inner_block_function_6__14_2), ._15(inner_block_function_6__15_2),
    ._0_2(inner_block_function_7__0_2), ._1_2(inner_block_function_7__1_2),
    ._2_2(inner_block_function_7__2_2), ._3_2(inner_block_function_7__3_2),
    ._4_2(inner_block_function_7__4_2), ._5_2(inner_block_function_7__5_2),
    ._6_2(inner_block_function_7__6_2), ._7_2(inner_block_function_7__7_2),
    ._8_2(inner_block_function_7__8_2), ._9_2(inner_block_function_7__9_2),
    ._10_2(inner_block_function_7__10_2), ._11_2(inner_block_function_7__11_2),
    ._12_2(inner_block_function_7__12_2), ._13_2(inner_block_function_7__13_2),
    ._14_2(inner_block_function_7__14_2), ._15_2(inner_block_function_7__15_2));
  inner_block_function inner_block_function_8 (
    ._0(inner_block_function_7__0_2), ._1(inner_block_function_7__1_2), ._2(inner_block_function_7__2_2),
    ._3(inner_block_function_7__3_2), ._4(inner_block_function_7__4_2), ._5(inner_block_function_7__5_2),
    ._6(inner_block_function_7__6_2), ._7(inner_block_function_7__7_2), ._8(inner_block_function_7__8_2),
    ._9(inner_block_function_7__9_2), ._10(inner_block_function_7__10_2), ._11(inner_block_function_7__11_2),
    ._12(inner_block_function_7__12_2), ._13(inner_block_function_7__13_2),
    ._14(inner_block_function_7__14_2), ._15(inner_block_function_7__15_2),
    ._0_2(inner_block_function_8__0_2), ._1_2(inner_block_function_8__1_2),
    ._2_2(inner_block_function_8__2_2), ._3_2(inner_block_function_8__3_2),
    ._4_2(inner_block_function_8__4_2), ._5_2(inner_block_function_8__5_2),
    ._6_2(inner_block_function_8__6_2), ._7_2(inner_block_function_8__7_2),
    ._8_2(inner_block_function_8__8_2), ._9_2(inner_block_function_8__9_2),
    ._10_2(inner_block_function_8__10_2), ._11_2(inner_block_function_8__11_2),
    ._12_2(inner_block_function_8__12_2), ._13_2(inner_block_function_8__13_2),
    ._14_2(inner_block_function_8__14_2), ._15_2(inner_block_function_8__15_2));
  inner_block_function inner_block_function_9 (
    ._0(inner_block_function_8__0_2), ._1(inner_block_function_8__1_2), ._2(inner_block_function_8__2_2),
    ._3(inner_block_function_8__3_2), ._4(inner_block_function_8__4_2), ._5(inner_block_function_8__5_2),
    ._6(inner_block_function_8__6_2), ._7(inner_block_function_8__7_2), ._8(inner_block_function_8__8_2),
    ._9(inner_block_function_8__9_2), ._10(inner_block_function_8__10_2), ._11(inner_block_function_8__11_2),
    ._12(inner_block_function_8__12_2), ._13(inner_block_function_8__13_2),
    ._14(inner_block_function_8__14_2), ._15(inner_block_function_8__15_2),
    ._0_2(inner_block_function_9__0_2), ._1_2(inner_block_function_9__1_2),
    ._2_2(inner_block_function_9__2_2), ._3_2(inner_block_function_9__3_2),
    ._4_2(inner_block_function_9__4_2), ._5_2(inner_block_function_9__5_2),
    ._6_2(inner_block_function_9__6_2), ._7_2(inner_block_function_9__7_2),
    ._8_2(inner_block_function_9__8_2), ._9_2(inner_block_function_9__9_2),
    ._10_2(inner_block_function_9__10_2), ._11_2(inner_block_function_9__11_2),
    ._12_2(inner_block_function_9__12_2), ._13_2(inner_block_function_9__13_2),
    ._14_2(inner_block_function_9__14_2), ._15_2(inner_block_function_9__15_2));
  inner_block_function inner_block_function_10 (
    ._0(inner_block_function_9__0_2), ._1(inner_block_function_9__1_2), ._2(inner_block_function_9__2_2),
    ._3(inner_block_function_9__3_2), ._4(inner_block_function_9__4_2), ._5(inner_block_function_9__5_2),
    ._6(inner_block_function_9__6_2), ._7(inner_block_function_9__7_2), ._8(inner_block_function_9__8_2),
    ._9(inner_block_function_9__9_2), ._10(inner_block_function_9__10_2), ._11(inner_block_function_9__11_2),
    ._12(inner_block_function_9__12_2), ._13(inner_block_function_9__13_2),
    ._14(inner_block_function_9__14_2), ._15(inner_block_function_9__15_2), ._0_2(o0), ._1_2(o1), ._2_2(o2),
    ._3_2(o3), ._4_2(o4), ._5_2(o5), ._6_2(o6), ._7_2(o7), ._8_2(o8), ._9_2(o9), ._10_2(o10), ._11_2(o11),
    ._12_2(o12), ._13_2(o13), ._14_2(o14), ._15_2(o15));

  // Notes on the sheet:
  //   MUST be needed to convert each output to little endian
endmodule

/* Test case test0:
k0 k1 k2 k3 k4 k5 k6 k7 bc n0 n1 n2 o0 o1 o2 o3 o4 o5 o6 o7 o8 o9 o10 o11 o12 o13 o14 o15

# RFC 8439 2.3.2 - ChaCha20 block, state after 20 rounds (before adding original state)
0x03020100 0x07060504 0x0b0a0908 0x0f0e0d0c 0x13121110 0x17161514 0x1b1a1918 0x1f1e1d1c 0x00000001 0x09000000 0x4a000000 0x00000000 0x837778ab 0xe238d763 0xa67ae21e 0x5950bb2f 0xc4f2d0c7 0xfc62bb2f 0x8fa018fc 0x3f5ec7b7 0x335271c2 0xf29489f3 0xeabda8fc 0x82e46ebd 0xd19c12b4 0xb04e16de 0x9e83d0cb 0x4e3c50a2
*/
