// Digital circuit inner_block_function.dig as structural Verilog
module inner_block_function (
  input  [31:0] _0,
  input  [31:0] _1,
  input  [31:0] _2,
  input  [31:0] _3,
  input  [31:0] _4,
  input  [31:0] _5,
  input  [31:0] _6,
  input  [31:0] _7,
  input  [31:0] _8,
  input  [31:0] _9,
  input  [31:0] _10,
  input  [31:0] _11,
  input  [31:0] _12,
  input  [31:0] _13,
  input  [31:0] _14,
  input  [31:0] _15,
  output [31:0] _0_2,
  output [31:0] _1_2,
  output [31:0] _2_2,
  output [31:0] _3_2,
  output [31:0] _4_2,
  output [31:0] _5_2,
  output [31:0] _6_2,
  output [31:0] _7_2,
  output [31:0] _8_2,
  output [31:0] _9_2,
  output [31:0] _10_2,
  output [31:0] _11_2,
  output [31:0] _12_2,
  output [31:0] _13_2,
  output [31:0] _14_2,
  output [31:0] _15_2
);

  wire [31:0] state_quarter_round_1_o0, state_quarter_round_1_o1, state_quarter_round_1_o2,
       state_quarter_round_1_o3, state_quarter_round_1_o4, state_quarter_round_1_o5,
       state_quarter_round_1_o6, state_quarter_round_1_o7, state_quarter_round_1_o8,
       state_quarter_round_1_o9, state_quarter_round_1_o10, state_quarter_round_1_o11,
       state_quarter_round_1_o12, state_quarter_round_1_o13, state_quarter_round_1_o14,
       state_quarter_round_1_o15, state_quarter_round_2_o0, state_quarter_round_2_o1,
       state_quarter_round_2_o2, state_quarter_round_2_o3, state_quarter_round_2_o4,
       state_quarter_round_2_o5, state_quarter_round_2_o6, state_quarter_round_2_o7,
       state_quarter_round_2_o8, state_quarter_round_2_o9, state_quarter_round_2_o10,
       state_quarter_round_2_o11, state_quarter_round_2_o12, state_quarter_round_2_o13,
       state_quarter_round_2_o14, state_quarter_round_2_o15, state_quarter_round_3_o0,
       state_quarter_round_3_o1, state_quarter_round_3_o2, state_quarter_round_3_o3,
       state_quarter_round_3_o4, state_quarter_round_3_o5, state_quarter_round_3_o6,
       state_quarter_round_3_o7, state_quarter_round_3_o8, state_quarter_round_3_o9,
       state_quarter_round_3_o10, state_quarter_round_3_o11, state_quarter_round_3_o12,
       state_quarter_round_3_o13, state_quarter_round_3_o14, state_quarter_round_3_o15,
       state_quarter_round_4_o0, state_quarter_round_4_o1, state_quarter_round_4_o2,
       state_quarter_round_4_o3, state_quarter_round_4_o4, state_quarter_round_4_o5,
       state_quarter_round_4_o6, state_quarter_round_4_o7, state_quarter_round_4_o8,
       state_quarter_round_4_o9, state_quarter_round_4_o10, state_quarter_round_4_o11,
       state_quarter_round_4_o12, state_quarter_round_4_o13, state_quarter_round_4_o14,
       state_quarter_round_4_o15, state_quarter_round_5_o0, state_quarter_round_5_o1,
       state_quarter_round_5_o2, state_quarter_round_5_o3, state_quarter_round_5_o4,
       state_quarter_round_5_o5, state_quarter_round_5_o6, state_quarter_round_5_o7,
       state_quarter_round_5_o8, state_quarter_round_5_o9, state_quarter_round_5_o10,
       state_quarter_round_5_o11, state_quarter_round_5_o12, state_quarter_round_5_o13,
       state_quarter_round_5_o14, state_quarter_round_5_o15, state_quarter_round_6_o0,
       state_quarter_round_6_o1, state_quarter_round_6_o2, state_quarter_round_6_o3,
       state_quarter_round_6_o4, state_quarter_round_6_o5, state_quarter_round_6_o6,
       state_quarter_round_6_o7, state_quarter_round_6_o8, state_quarter_round_6_o9,
       state_quarter_round_6_o10, state_quarter_round_6_o11, state_quarter_round_6_o12,
       state_quarter_round_6_o13, state_quarter_round_6_o14, state_quarter_round_6_o15,
       state_quarter_round_7_o0, state_quarter_round_7_o1, state_quarter_round_7_o2,
       state_quarter_round_7_o3, state_quarter_round_7_o4, state_quarter_round_7_o5,
       state_quarter_round_7_o6, state_quarter_round_7_o7, state_quarter_round_7_o8,
       state_quarter_round_7_o9, state_quarter_round_7_o10, state_quarter_round_7_o11,
       state_quarter_round_7_o12, state_quarter_round_7_o13, state_quarter_round_7_o14,
       state_quarter_round_7_o15;

  state_quarter_round state_quarter_round_1 (
    .i0(_0), .i1(_1), .i2(_2), .i3(_3), .i4(_4), .i5(_5), .i6(_6), .i7(_7), .i8(_8), .i9(_9), .i10(_10),
    .i11(_11), .i12(_12), .i13(_13), .i14(_14), .i15(_15), .x(4'b0000), .y(4'b0100), .z(4'b1000),
    .w(4'b1100), .o0(state_quarter_round_1_o0), .o1(state_quarter_round_1_o1), .o2(state_quarter_round_1_o2),
    .o3(state_quarter_round_1_o3), .o4(state_quarter_round_1_o4), .o5(state_quarter_round_1_o5),
    .o6(state_quarter_round_1_o6), .o7(state_quarter_round_1_o7), .o8(state_quarter_round_1_o8),
    .o9(state_quarter_round_1_o9), .o10(state_quarter_round_1_o10), .o11(state_quarter_round_1_o11),
    .o12(state_quarter_round_1_o12), .o13(state_quarter_round_1_o13), .o14(state_quarter_round_1_o14),
    .o15(state_quarter_round_1_o15));
  state_quarter_round state_quarter_round_2 (
    .i0(state_quarter_round_1_o0), .i1(state_quarter_round_1_o1), .i2(state_quarter_round_1_o2),
    .i3(state_quarter_round_1_o3), .i4(state_quarter_round_1_o4), .i5(state_quarter_round_1_o5),
    .i6(state_quarter_round_1_o6), .i7(state_quarter_round_1_o7), .i8(state_quarter_round_1_o8),
    .i9(state_quarter_round_1_o9), .i10(state_quarter_round_1_o10), .i11(state_quarter_round_1_o11),
    .i12(state_quarter_round_1_o12), .i13(state_quarter_round_1_o13), .i14(state_quarter_round_1_o14),
    .i15(state_quarter_round_1_o15), .x(4'b0001), .y(4'b0101), .z(4'b1001), .w(4'b1101),
    .o0(state_quarter_round_2_o0), .o1(state_quarter_round_2_o1), .o2(state_quarter_round_2_o2),
    .o3(state_quarter_round_2_o3), .o4(state_quarter_round_2_o4), .o5(state_quarter_round_2_o5),
    .o6(state_quarter_round_2_o6), .o7(state_quarter_round_2_o7), .o8(state_quarter_round_2_o8),
    .o9(state_quarter_round_2_o9), .o10(state_quarter_round_2_o10), .o11(state_quarter_round_2_o11),
    .o12(state_quarter_round_2_o12), .o13(state_quarter_round_2_o13), .o14(state_quarter_round_2_o14),
    .o15(state_quarter_round_2_o15));
  state_quarter_round state_quarter_round_3 (
    .i0(state_quarter_round_2_o0), .i1(state_quarter_round_2_o1), .i2(state_quarter_round_2_o2),
    .i3(state_quarter_round_2_o3), .i4(state_quarter_round_2_o4), .i5(state_quarter_round_2_o5),
    .i6(state_quarter_round_2_o6), .i7(state_quarter_round_2_o7), .i8(state_quarter_round_2_o8),
    .i9(state_quarter_round_2_o9), .i10(state_quarter_round_2_o10), .i11(state_quarter_round_2_o11),
    .i12(state_quarter_round_2_o12), .i13(state_quarter_round_2_o13), .i14(state_quarter_round_2_o14),
    .i15(state_quarter_round_2_o15), .x(4'b0010), .y(4'b0110), .z(4'b1010), .w(4'b1110),
    .o0(state_quarter_round_3_o0), .o1(state_quarter_round_3_o1), .o2(state_quarter_round_3_o2),
    .o3(state_quarter_round_3_o3), .o4(state_quarter_round_3_o4), .o5(state_quarter_round_3_o5),
    .o6(state_quarter_round_3_o6), .o7(state_quarter_round_3_o7), .o8(state_quarter_round_3_o8),
    .o9(state_quarter_round_3_o9), .o10(state_quarter_round_3_o10), .o11(state_quarter_round_3_o11),
    .o12(state_quarter_round_3_o12), .o13(state_quarter_round_3_o13), .o14(state_quarter_round_3_o14),
    .o15(state_quarter_round_3_o15));
  state_quarter_round state_quarter_round_4 (
    .i0(state_quarter_round_3_o0), .i1(state_quarter_round_3_o1), .i2(state_quarter_round_3_o2),
    .i3(state_quarter_round_3_o3), .i4(state_quarter_round_3_o4), .i5(state_quarter_round_3_o5),
    .i6(state_quarter_round_3_o6), .i7(state_quarter_round_3_o7), .i8(state_quarter_round_3_o8),
    .i9(state_quarter_round_3_o9), .i10(state_quarter_round_3_o10), .i11(state_quarter_round_3_o11),
    .i12(state_quarter_round_3_o12), .i13(state_quarter_round_3_o13), .i14(state_quarter_round_3_o14),
    .i15(state_quarter_round_3_o15), .x(4'b0011), .y(4'b0111), .z(4'b1011), .w(4'b1111),
    .o0(state_quarter_round_4_o0), .o1(state_quarter_round_4_o1), .o2(state_quarter_round_4_o2),
    .o3(state_quarter_round_4_o3), .o4(state_quarter_round_4_o4), .o5(state_quarter_round_4_o5),
    .o6(state_quarter_round_4_o6), .o7(state_quarter_round_4_o7), .o8(state_quarter_round_4_o8),
    .o9(state_quarter_round_4_o9), .o10(state_quarter_round_4_o10), .o11(state_quarter_round_4_o11),
    .o12(state_quarter_round_4_o12), .o13(state_quarter_round_4_o13), .o14(state_quarter_round_4_o14),
    .o15(state_quarter_round_4_o15));
  state_quarter_round state_quarter_round_5 (
    .i0(state_quarter_round_4_o0), .i1(state_quarter_round_4_o1), .i2(state_quarter_round_4_o2),
    .i3(state_quarter_round_4_o3), .i4(state_quarter_round_4_o4), .i5(state_quarter_round_4_o5),
    .i6(state_quarter_round_4_o6), .i7(state_quarter_round_4_o7), .i8(state_quarter_round_4_o8),
    .i9(state_quarter_round_4_o9), .i10(state_quarter_round_4_o10), .i11(state_quarter_round_4_o11),
    .i12(state_quarter_round_4_o12), .i13(state_quarter_round_4_o13), .i14(state_quarter_round_4_o14),
    .i15(state_quarter_round_4_o15), .x(4'b0000), .y(4'b0101), .z(4'b1010), .w(4'b1111),
    .o0(state_quarter_round_5_o0), .o1(state_quarter_round_5_o1), .o2(state_quarter_round_5_o2),
    .o3(state_quarter_round_5_o3), .o4(state_quarter_round_5_o4), .o5(state_quarter_round_5_o5),
    .o6(state_quarter_round_5_o6), .o7(state_quarter_round_5_o7), .o8(state_quarter_round_5_o8),
    .o9(state_quarter_round_5_o9), .o10(state_quarter_round_5_o10), .o11(state_quarter_round_5_o11),
    .o12(state_quarter_round_5_o12), .o13(state_quarter_round_5_o13), .o14(state_quarter_round_5_o14),
    .o15(state_quarter_round_5_o15));
  state_quarter_round state_quarter_round_6 (
    .i0(state_quarter_round_5_o0), .i1(state_quarter_round_5_o1), .i2(state_quarter_round_5_o2),
    .i3(state_quarter_round_5_o3), .i4(state_quarter_round_5_o4), .i5(state_quarter_round_5_o5),
    .i6(state_quarter_round_5_o6), .i7(state_quarter_round_5_o7), .i8(state_quarter_round_5_o8),
    .i9(state_quarter_round_5_o9), .i10(state_quarter_round_5_o10), .i11(state_quarter_round_5_o11),
    .i12(state_quarter_round_5_o12), .i13(state_quarter_round_5_o13), .i14(state_quarter_round_5_o14),
    .i15(state_quarter_round_5_o15), .x(4'b0001), .y(4'b0110), .z(4'b1011), .w(4'b1100),
    .o0(state_quarter_round_6_o0), .o1(state_quarter_round_6_o1), .o2(state_quarter_round_6_o2),
    .o3(state_quarter_round_6_o3), .o4(state_quarter_round_6_o4), .o5(state_quarter_round_6_o5),
    .o6(state_quarter_round_6_o6), .o7(state_quarter_round_6_o7), .o8(state_quarter_round_6_o8),
    .o9(state_quarter_round_6_o9), .o10(state_quarter_round_6_o10), .o11(state_quarter_round_6_o11),
    .o12(state_quarter_round_6_o12), .o13(state_quarter_round_6_o13), .o14(state_quarter_round_6_o14),
    .o15(state_quarter_round_6_o15));
  state_quarter_round state_quarter_round_7 (
    .i0(state_quarter_round_6_o0), .i1(state_quarter_round_6_o1), .i2(state_quarter_round_6_o2),
    .i3(state_quarter_round_6_o3), .i4(state_quarter_round_6_o4), .i5(state_quarter_round_6_o5),
    .i6(state_quarter_round_6_o6), .i7(state_quarter_round_6_o7), .i8(state_quarter_round_6_o8),
    .i9(state_quarter_round_6_o9), .i10(state_quarter_round_6_o10), .i11(state_quarter_round_6_o11),
    .i12(state_quarter_round_6_o12), .i13(state_quarter_round_6_o13), .i14(state_quarter_round_6_o14),
    .i15(state_quarter_round_6_o15), .x(4'b0010), .y(4'b0111), .z(4'b1000), .w(4'b1101),
    .o0(state_quarter_round_7_o0), .o1(state_quarter_round_7_o1), .o2(state_quarter_round_7_o2),
    .o3(state_quarter_round_7_o3), .o4(state_quarter_round_7_o4), .o5(state_quarter_round_7_o5),
    .o6(state_quarter_round_7_o6), .o7(state_quarter_round_7_o7), .o8(state_quarter_round_7_o8),
    .o9(state_quarter_round_7_o9), .o10(state_quarter_round_7_o10), .o11(state_quarter_round_7_o11),
    .o12(state_quarter_round_7_o12), .o13(state_quarter_round_7_o13), .o14(state_quarter_round_7_o14),
    .o15(state_quarter_round_7_o15));
  state_quarter_round state_quarter_round_8 (
    .i0(state_quarter_round_7_o0), .i1(state_quarter_round_7_o1), .i2(state_quarter_round_7_o2),
    .i3(state_quarter_round_7_o3), .i4(state_quarter_round_7_o4), .i5(state_quarter_round_7_o5),
    .i6(state_quarter_round_7_o6), .i7(state_quarter_round_7_o7), .i8(state_quarter_round_7_o8),
    .i9(state_quarter_round_7_o9), .i10(state_quarter_round_7_o10), .i11(state_quarter_round_7_o11),
    .i12(state_quarter_round_7_o12), .i13(state_quarter_round_7_o13), .i14(state_quarter_round_7_o14),
    .i15(state_quarter_round_7_o15), .x(4'b0011), .y(4'b0100), .z(4'b1001), .w(4'b1110), .o0(_0_2),
    .o1(_1_2), .o2(_2_2), .o3(_3_2), .o4(_4_2), .o5(_5_2), .o6(_6_2), .o7(_7_2), .o8(_8_2), .o9(_9_2),
    .o10(_10_2), .o11(_11_2), .o12(_12_2), .o13(_13_2), .o14(_14_2), .o15(_15_2));
endmodule
