// Digital circuit quarter_round.dig as structural Verilog
module quarter_round (
  input  [31:0] a,
  input  [31:0] b,
  input  [31:0] c,
  input  [31:0] d,
  output [31:0] A_2,
  output [31:0] B_2,
  output [31:0] C_2,
  output [31:0] D_2
);

  wire [31:0] add_1_s, add_3_s, barrelshifter_1_out, barrelshifter_3_out, xor_1_out, xor_2_out, xor_3_out,
       xor_4_out;

  Add #(.Bits(32)) add_1 (.a(a), .b(b), .s(add_1_s));  // open: c_i, c_o
  Add #(.Bits(32)) add_2 (.a(add_1_s), .b(barrelshifter_3_out), .s(A_2));  // open: c_i, c_o
  assign xor_1_out = add_1_s ^ d;  // XOr xor_1, 32 bits wide
  assign xor_2_out = A_2 ^ barrelshifter_1_out;  // XOr xor_2, 32 bits wide
  BarrelShifter #(.Bits(32), .barrelShifterMode("rotate")) barrelshifter_1 (
    .in(xor_1_out), .shift(32'h10), .out(barrelshifter_1_out));
  BarrelShifter #(.Bits(32), .barrelShifterMode("rotate")) barrelshifter_2 (.in(xor_2_out), .shift(32'h8), .out(D_2));
  Add #(.Bits(32)) add_3 (.a(barrelshifter_1_out), .b(c), .s(add_3_s));  // open: c_i, c_o
  Add #(.Bits(32)) add_4 (.a(D_2), .b(add_3_s), .s(C_2));  // open: c_i, c_o
  assign xor_3_out = add_3_s ^ b;  // XOr xor_3, 32 bits wide
  assign xor_4_out = C_2 ^ barrelshifter_3_out;  // XOr xor_4, 32 bits wide
  BarrelShifter #(.Bits(32), .barrelShifterMode("rotate")) barrelshifter_3 (
    .in(xor_3_out), .shift(32'hc), .out(barrelshifter_3_out));
  BarrelShifter #(.Bits(32), .barrelShifterMode("rotate")) barrelshifter_4 (.in(xor_4_out), .shift(32'h7), .out(B_2));

  // Notes on the sheet:
  //   The ChaCha Quarter Round
  //   inputs
  //   a+=b
  //   a
  //   d\^=a
  //   d<<<=16
  //   d
  //   c+=d
  //   c
  //   b\^=c
  //   b<<<=12
  //   b
endmodule
